# Fritzing sketch wiring-diagram (saved by Fritzing 0.9.3b)
breadboards: 2

parts:
  Raspberry_Pi1 = Raspberry Pi 2
  Disp1 = LBT2088AH [part_number=LBT2088AH]
  S5 = Pushbutton [package="[THT]"]
  S6 = Pushbutton [package="[THT]"]
  S7 = Pushbutton [package="[THT]"]
  R3 = Resistor [tolerance=±5% resistance=1k package="0402 [SMD]"]
  R4 = Resistor [tolerance=±5% resistance=1k package="0402 [SMD]"]
  R5 = Resistor [tolerance=±5% resistance=1k package="0402 [SMD]"]
  R6 = Resistor [tolerance=±5% resistance=1k package="0402 [SMD]"]
  R7 = Resistor [tolerance=±5% resistance=1k package="0402 [SMD]"]
  R8 = Resistor [tolerance=±5% resistance=1k package="0402 [SMD]"]
  R9 = Resistor [tolerance=±5% resistance=1k package="0402 [SMD]"]
  R10 = Resistor [tolerance=±5% resistance=1k package="0402 [SMD]"]

nets:
  3V3: Raspberry_Pi1.3v3, Raspberry_Pi1.GPIO2, Raspberry_Pi1.3V3, Raspberry_Pi1.GPIO24, Raspberry_Pi1.5V, S5.Pin_3, S5.Pin_4, S6.Pin_1, S6.Pin_2, S6.Pin_3, S6.Pin_4, S7.Pin_3, S7.Pin_4
  N1: Raspberry_Pi1.GPIO3, Raspberry_Pi1.GPIO4, Raspberry_Pi1.GND, Raspberry_Pi1.GPIO11, Raspberry_Pi1.GPIO5, Raspberry_Pi1.GPIO13, Raspberry_Pi1.GPIO18, Disp1.pin2, Disp1.pin_3, Disp1.pin_13, Disp1.pin_14, Disp1.pin_16, S5.Pin_1, S5.Pin_2, R3.Pin_0, R3.Pin_1, R6.Pin_0, R6.Pin_1, R8.Pin_0, R8.Pin_1
  N2: Raspberry_Pi1.GPIO17, Raspberry_Pi1.GPIO27, Disp1.pin_8
  N3: Raspberry_Pi1.GPIO22, Raspberry_Pi1.GPIO23, S7.Pin_1, S7.Pin_2
  N4: Raspberry_Pi1.GPIO10, Disp1.pin_15, R7.Pin_0, R7.Pin_1
  N5: Raspberry_Pi1.GPIO9, Raspberry_Pi1.GPIO25, Disp1.pin_11, R9.Pin_0, R9.Pin_1
  N6: Raspberry_Pi1.GPIO6, Disp1.pin_4, R4.Pin_0, R4.Pin_1
  N7: Raspberry_Pi1.GPIO19, Raspberry_Pi1.GPIO26, Disp1.pin_9
  N8: Raspberry_Pi1.GPIO20, Raspberry_Pi1.GPIO16, Disp1.pin_12
  N9: Raspberry_Pi1.GPIO12, Disp1.pin_5
  N10: Raspberry_Pi1.ID_SC, Raspberry_Pi1.GPIO7, Disp1.pin_10, R10.Pin_0, R10.Pin_1
  N11: Raspberry_Pi1.GPIO8, Disp1.pin_6, R5.Pin_0, R5.Pin_1
  N12: Raspberry_Pi1.GPIO15, Disp1.pin1
  N13: Raspberry_Pi1.GPIO14, Disp1.pin_7

notes:
  マイクとスピーカーを接続する
  OSL641501-ARA
  品番が書いてある方を下向きにする
  Pinの並びは以下になる
  16, 15, 14, 13, 12, 11, 10, 9
  1, 2, 3, 4, 5, 6, 7, 8
  Red : Prev
  Green : Start or Pause
  Blue : Next
